// Logisim project cpu.circ as structural Verilog: 3 circuits, main circuit main
module main (
  output [7:0] out_1
);

  wire and_1_out, clock_1_out, cond_1_cout, controlled_buffer_1_out, decoder_1_out0, decoder_1_out1,
       decoder_1_out2, decoder_1_out3, decoder_1_out4, decoder_1_out5, decoder_1_out6, decoder_2_out0,
       decoder_2_out1, decoder_2_out2, decoder_2_out3, decoder_2_out4, decoder_2_out5, decoder_3_out0,
       decoder_3_out1, decoder_3_out2, decoder_3_out3, or_1_out, or_2_out;
  wire [1:0] rom_1_data;
  wire [2:0] rom_1_data_3;
  wire [5:3] rom_1_data_2;
  wire [7:0] A_q, alu_1_aout, B_q, C_q, controlled_buffer_2_out, controlled_buffer_3_out, counter_1_q, D_q,
       E_q, F_q;

  Cond cond_1 (.condin(rom_1_data_3), .inbits(D_q), .Cout(cond_1_cout));
  assign controlled_buffer_1_out = and_1_out ? decoder_3_out3 : 1'bz;  // Controlled_Buffer controlled_buffer_1
  and and_1 (and_1_out, cond_1_cout, decoder_3_out3);
  Counter #(.trigger("falling")) counter_1 (
    .load(controlled_buffer_1_out), .clk(clock_1_out), .D(controlled_buffer_2_out), .Q(counter_1_q));  // open: clr, up, count, carry
  Clock clock_1 (.out(clock_1_out));
  assign controlled_buffer_2_out = and_1_out ? A_q : 8'bz;  // Controlled_Buffer controlled_buffer_2
  ROM rom_1 (.addr(counter_1_q), .data({rom_1_data, rom_1_data_2, rom_1_data_3}));
  Decoder #(.select(3)) decoder_1 (
    .out0(decoder_1_out0), .out1(decoder_1_out1), .out2(decoder_1_out2), .out3(decoder_1_out3),
    .out4(decoder_1_out4), .out5(decoder_1_out5), .out6(decoder_1_out6), .sel(rom_1_data_2),
    .en(decoder_3_out2));  // open: out7
  Decoder #(.select(3)) decoder_2 (
    .out0(decoder_2_out0), .out1(decoder_2_out1), .out2(decoder_2_out2), .out3(decoder_2_out3),
    .out4(decoder_2_out4), .out5(decoder_2_out5), .sel(rom_1_data_3), .en(decoder_3_out2));  // open: out6, out7
  Decoder #(.select(2)) decoder_3 (
    .out0(decoder_3_out0), .out1(decoder_3_out1), .out2(decoder_3_out2), .out3(decoder_3_out3),
    .sel(rom_1_data));  // open: en
  or or_1 (or_1_out, decoder_1_out0, decoder_3_out0);
  or or_2 (or_2_out, decoder_3_out1, decoder_1_out3);
  assign controlled_buffer_3_out = decoder_3_out0 ? {rom_1_data, rom_1_data_2, rom_1_data_3} : 8'bz;  // Controlled_Buffer controlled_buffer_3
  Register A (.D(controlled_buffer_3_out), .en(or_1_out), .clk(clock_1_out), .Q(A_q));  // open: clr
  Register B (.D(controlled_buffer_3_out), .en(decoder_1_out1), .clk(clock_1_out), .Q(B_q));  // open: clr
  Register C (.D(controlled_buffer_3_out), .en(decoder_1_out2), .clk(clock_1_out), .Q(C_q));  // open: clr
  Register D (.D(controlled_buffer_3_out), .en(or_2_out), .clk(clock_1_out), .Q(D_q));  // open: clr
  Register E (.D(controlled_buffer_3_out), .en(decoder_1_out4), .clk(clock_1_out), .Q(E_q));  // open: clr
  Register F (.D(controlled_buffer_3_out), .en(decoder_1_out5), .clk(clock_1_out), .Q(F_q));  // open: clr
  assign controlled_buffer_3_out = decoder_2_out0 ? A_q : 8'bz;  // Controlled_Buffer controlled_buffer_4
  assign controlled_buffer_3_out = decoder_2_out1 ? B_q : 8'bz;  // Controlled_Buffer controlled_buffer_5
  assign controlled_buffer_3_out = decoder_2_out2 ? C_q : 8'bz;  // Controlled_Buffer controlled_buffer_6
  assign controlled_buffer_3_out = decoder_2_out3 ? D_q : 8'bz;  // Controlled_Buffer controlled_buffer_7
  assign controlled_buffer_3_out = decoder_2_out4 ? E_q : 8'bz;  // Controlled_Buffer controlled_buffer_8
  assign controlled_buffer_3_out = decoder_2_out5 ? F_q : 8'bz;  // Controlled_Buffer controlled_buffer_9
  ALU alu_1 (.Op(rom_1_data_3), .A(B_q), .B(C_q), .Aout(alu_1_aout));
  assign controlled_buffer_3_out = decoder_3_out1 ? alu_1_aout : 8'bz;  // Controlled_Buffer controlled_buffer_10
  assign out_1 = decoder_1_out6 ? controlled_buffer_3_out : 8'bz;  // Controlled_Buffer controlled_buffer_11

  // Notes on the sheet:
  //   contents of rom_1 (hex, n*v repeats v):
  //   4 a0 4 c1 8c 1 90 45 d c2 a3 4 c1
  //   imm
  //   alu
  //   mov
  //   cond
endmodule

module ALU (
  input  [2:0] Op,
  input  [7:0] A,
  input  [7:0] B,
  output [7:0] Aout
);

  wire decoder_1_out0, decoder_1_out1, decoder_1_out2, decoder_1_out3, decoder_1_out4, decoder_1_out5,
       decoder_1_out6, decoder_1_out7;
  wire [7:0] adder_1_out, and_1_out, nand_1_out, nor_1_out, not_1_out, or_1_out, subtractor_1_out, xor_1_out;

  Decoder #(.select(3)) decoder_1 (
    .out0(decoder_1_out0), .out1(decoder_1_out1), .out2(decoder_1_out2), .out3(decoder_1_out3),
    .out4(decoder_1_out4), .out5(decoder_1_out5), .out6(decoder_1_out6), .out7(decoder_1_out7), .sel(Op));  // open: en
  assign nand_1_out = ~(A & B);  // NAND_Gate nand_1, 8 bits wide
  assign Aout = decoder_1_out0 ? nand_1_out : 8'bz;  // Controlled_Buffer controlled_buffer_1
  assign or_1_out = B | A;  // OR_Gate or_1, 8 bits wide
  assign Aout = decoder_1_out1 ? or_1_out : 8'bz;  // Controlled_Buffer controlled_buffer_2
  assign and_1_out = B & A;  // AND_Gate and_1, 8 bits wide
  assign Aout = decoder_1_out2 ? and_1_out : 8'bz;  // Controlled_Buffer controlled_buffer_3
  assign nor_1_out = ~(B | A);  // NOR_Gate nor_1, 8 bits wide
  assign Aout = decoder_1_out3 ? nor_1_out : 8'bz;  // Controlled_Buffer controlled_buffer_4
  assign Aout = decoder_1_out4 ? adder_1_out : 8'bz;  // Controlled_Buffer controlled_buffer_5
  Adder adder_1 (.a(B), .b(A), .out(adder_1_out));  // open: cin, cout
  assign Aout = decoder_1_out5 ? subtractor_1_out : 8'bz;  // Controlled_Buffer controlled_buffer_6
  Subtractor subtractor_1 (.a(A), .b(B), .out(subtractor_1_out));  // open: bin, bout
  assign xor_1_out = B ^ A;  // XOR_Gate xor_1, 8 bits wide
  assign Aout = decoder_1_out6 ? xor_1_out : 8'bz;  // Controlled_Buffer controlled_buffer_7
  assign not_1_out = ~A;  // NOT_Gate not_1, 8 bits wide
  assign Aout = decoder_1_out7 ? not_1_out : 8'bz;  // Controlled_Buffer controlled_buffer_8
endmodule

module Cond (
  input  [2:0] condin,
  input  [7:0] inbits,
  output Cout
);

  wire comparator_1_eq, comparator_1_gt, comparator_1_lt, decoder_1_out0, decoder_1_out1, decoder_1_out2,
       decoder_1_out3, decoder_1_out4, decoder_1_out5, decoder_1_out6, decoder_1_out7, not_1_out, or_1_out,
       or_2_out, or_3_out;

  Decoder #(.select(3)) decoder_1 (
    .out0(decoder_1_out0), .out1(decoder_1_out1), .out2(decoder_1_out2), .out3(decoder_1_out3),
    .out4(decoder_1_out4), .out5(decoder_1_out5), .out6(decoder_1_out6), .out7(decoder_1_out7), .sel(condin));  // open: en
  assign Cout = decoder_1_out0 ? 1'b0 : 1'bz;  // Controlled_Buffer controlled_buffer_1
  assign Cout = decoder_1_out1 ? or_1_out : 1'bz;  // Controlled_Buffer controlled_buffer_2
  or or_1 (or_1_out, comparator_1_gt, comparator_1_eq, comparator_1_lt);
  Comparator comparator_1 (.a(inbits), .b({8{1'b0}}), .gt(comparator_1_gt), .eq(comparator_1_eq), .lt(comparator_1_lt));
  assign Cout = decoder_1_out2 ? comparator_1_eq : 1'bz;  // Controlled_Buffer controlled_buffer_3
  assign Cout = decoder_1_out3 ? not_1_out : 1'bz;  // Controlled_Buffer controlled_buffer_4
  assign Cout = decoder_1_out4 ? comparator_1_lt : 1'bz;  // Controlled_Buffer controlled_buffer_5
  not not_1 (not_1_out, comparator_1_eq);
  assign Cout = decoder_1_out5 ? or_2_out : 1'bz;  // Controlled_Buffer controlled_buffer_6
  assign Cout = decoder_1_out6 ? or_3_out : 1'bz;  // Controlled_Buffer controlled_buffer_7
  or or_2 (or_2_out, comparator_1_eq, comparator_1_gt);
  or or_3 (or_3_out, comparator_1_lt, comparator_1_eq);
  assign Cout = decoder_1_out7 ? comparator_1_gt : 1'bz;  // Controlled_Buffer controlled_buffer_8
endmodule
